// Logisim project proyecto.circ as structural Verilog: 1 circuit, main circuit main
module main (
  input  A,
  input  B,
  input  C,
  input  D,
  output out_5
);

  wire and_1_out, and_2_out, not_1_out, or_1_out;

  and and_1 (and_1_out, A, B);
  or or_1 (or_1_out, C, D);
  and and_2 (and_2_out, and_1_out, or_1_out);
  not not_1 (not_1_out, D);
  or or_2 (out_5, and_2_out, not_1_out);

  // Notes on the sheet:
  //   A .B
  //   C+D
  //   A.B(C+D)
  //   AB(C+D)+D(complemento)
endmodule
